// Logisim project PROIECT_DSD.circ as structural Verilog
module main (
  input  [1:0] in_1,
  input  in_2,
  input  [1:0] in_3,
  output [7:0] out_4,
  output [3:0] out_5,
  output [6:0] out_6,
  output [7:0] out_7
);

  wire button_1_out;
  wire [3:0] decodificator_zecimal_1_sute, decodificator_zecimal_1_unitate, decodificator_zecimal_1_zecimala,
       decodificator_zecimal_2_sute, decodificator_zecimal_2_unitate, decodificator_zecimal_2_zecimala;
  wire [6:0] hex_7seg_1_a_b_c_d_e_f_g, hex_7seg_2_a_b_c_d_e_f_g, hex_7seg_3_a_b_c_d_e_f_g,
       hex_7seg_4_a_b_c_d_e_f_g, hex_7seg_5_a_b_c_d_e_f_g, hex_7seg_6_a_b_c_d_e_f_g;

  Button button_1 (.out(button_1_out));
  data_generator_block data_generator_block_1 (.CONTROL(in_1), .CLK(button_1_out), .RESET(in_2), .Data(out_4));
  average_computer_block average_computer_block_1 (
    .DIN(out_4), .CLK(button_1_out), .FILTER(in_3), .RESET(in_2), .AVERAGE(out_7));
  lcd_display lcd_display_1 (
    .CLK(button_1_out), .RESET(in_2), .DIN(out_4), .AVG(out_7), .ANODE(out_5), .CATHODE(out_6));
  decodificator_zecimal decodificator_zecimal_1 (
    .nr_bin(out_4), .Unitate(decodificator_zecimal_1_unitate), .Zecimala(decodificator_zecimal_1_zecimala),
    .Sute(decodificator_zecimal_1_sute));
  decodificator_zecimal decodificator_zecimal_2 (
    .nr_bin(out_7), .Unitate(decodificator_zecimal_2_unitate), .Zecimala(decodificator_zecimal_2_zecimala),
    .Sute(decodificator_zecimal_2_sute));
  hex_7seg hex_7seg_1 (.hex_in(decodificator_zecimal_1_sute), .a_b_c_d_e_f_g(hex_7seg_1_a_b_c_d_e_f_g));
  hex_7seg hex_7seg_2 (.hex_in(decodificator_zecimal_1_zecimala), .a_b_c_d_e_f_g(hex_7seg_2_a_b_c_d_e_f_g));
  hex_7seg hex_7seg_3 (.hex_in(decodificator_zecimal_1_unitate), .a_b_c_d_e_f_g(hex_7seg_3_a_b_c_d_e_f_g));
  hex_7seg hex_7seg_4 (.hex_in(decodificator_zecimal_2_sute), .a_b_c_d_e_f_g(hex_7seg_4_a_b_c_d_e_f_g));
  hex_7seg hex_7seg_5 (.hex_in(decodificator_zecimal_2_zecimala), .a_b_c_d_e_f_g(hex_7seg_5_a_b_c_d_e_f_g));
  hex_7seg hex_7seg_6 (.hex_in(decodificator_zecimal_2_unitate), .a_b_c_d_e_f_g(hex_7seg_6_a_b_c_d_e_f_g));
  _7_Segment_Display u_7_segment_display_1 (
    .g(hex_7seg_1_a_b_c_d_e_f_g[0]), .f(hex_7seg_1_a_b_c_d_e_f_g[1]), .a(hex_7seg_1_a_b_c_d_e_f_g[6]),
    .b(hex_7seg_1_a_b_c_d_e_f_g[5]), .e(hex_7seg_1_a_b_c_d_e_f_g[2]), .d(hex_7seg_1_a_b_c_d_e_f_g[3]),
    .c(hex_7seg_1_a_b_c_d_e_f_g[4]));  // open: dp
  _7_Segment_Display u_7_segment_display_2 (
    .g(hex_7seg_4_a_b_c_d_e_f_g[0]), .f(hex_7seg_4_a_b_c_d_e_f_g[1]), .a(hex_7seg_4_a_b_c_d_e_f_g[6]),
    .b(hex_7seg_4_a_b_c_d_e_f_g[5]), .e(hex_7seg_4_a_b_c_d_e_f_g[2]), .d(hex_7seg_4_a_b_c_d_e_f_g[3]),
    .c(hex_7seg_4_a_b_c_d_e_f_g[4]));  // open: dp
  _7_Segment_Display u_7_segment_display_3 (
    .g(hex_7seg_2_a_b_c_d_e_f_g[0]), .f(hex_7seg_2_a_b_c_d_e_f_g[1]), .a(hex_7seg_2_a_b_c_d_e_f_g[6]),
    .b(hex_7seg_2_a_b_c_d_e_f_g[5]), .e(hex_7seg_2_a_b_c_d_e_f_g[2]), .d(hex_7seg_2_a_b_c_d_e_f_g[3]),
    .c(hex_7seg_2_a_b_c_d_e_f_g[4]));  // open: dp
  _7_Segment_Display u_7_segment_display_4 (
    .g(hex_7seg_5_a_b_c_d_e_f_g[0]), .f(hex_7seg_5_a_b_c_d_e_f_g[1]), .a(hex_7seg_5_a_b_c_d_e_f_g[6]),
    .b(hex_7seg_5_a_b_c_d_e_f_g[5]), .e(hex_7seg_5_a_b_c_d_e_f_g[2]), .d(hex_7seg_5_a_b_c_d_e_f_g[3]),
    .c(hex_7seg_5_a_b_c_d_e_f_g[4]));  // open: dp
  _7_Segment_Display u_7_segment_display_5 (
    .g(hex_7seg_3_a_b_c_d_e_f_g[0]), .f(hex_7seg_3_a_b_c_d_e_f_g[1]), .a(hex_7seg_3_a_b_c_d_e_f_g[6]),
    .b(hex_7seg_3_a_b_c_d_e_f_g[5]), .e(hex_7seg_3_a_b_c_d_e_f_g[2]), .d(hex_7seg_3_a_b_c_d_e_f_g[3]),
    .c(hex_7seg_3_a_b_c_d_e_f_g[4]));  // open: dp
  _7_Segment_Display u_7_segment_display_6 (
    .g(hex_7seg_6_a_b_c_d_e_f_g[0]), .f(hex_7seg_6_a_b_c_d_e_f_g[1]), .a(hex_7seg_6_a_b_c_d_e_f_g[6]),
    .b(hex_7seg_6_a_b_c_d_e_f_g[5]), .e(hex_7seg_6_a_b_c_d_e_f_g[2]), .d(hex_7seg_6_a_b_c_d_e_f_g[3]),
    .c(hex_7seg_6_a_b_c_d_e_f_g[4]));  // open: dp
endmodule

// VHDL entity xor_gate, as the project stores it:
library ieee;
use ieee.std_logic_1164.all;

entity xor_gate is
    port (
        x, y : in std_logic;
        z : out std_logic
    );
end xor_gate;

architecture arch_xor of xor_gate is
begin
    z <= x xor y;
end arch_xor;

// VHDL entity squarewave_generator, as the project stores it:
library ieee;
use ieee.std_logic_1164.all;
use ieee.numeric_std.all;

entity squarewave_generator is
    port (
        clk: in std_logic;
        R: in std_logic;
        clk_out: out std_logic
    );
end squarewave_generator;

architecture arch_square of squarewave_generator is
    signal count: unsigned(1 downto 0) := "00";
begin
    process(clk, R)
    begin
        if R = '1' then
            count <= "00";
        elsif rising_edge(clk) then
            count <= count + 1;
        end if;
    end process;

    clk_out <= count(1);
end arch_square;

// VHDL entity lfsr_4bit, as the project stores it:
library ieee;
use ieee.std_logic_1164.all;

entity lfsr_4bit is
    port (
        CLK   : in  std_logic;
        Q     : out std_logic_vector(3 downto 0);
        RESET : in  std_logic
    );
end lfsr_4bit;

architecture arch_lfsr4 of lfsr_4bit is
    

    component xor_gate is
        port (
            x : in  std_logic;
            y : in  std_logic;
            z : out std_logic
        );
    end component;

    signal iQ      : std_logic_vector(3 downto 0) := "1111";
    signal rez_xor : std_logic;

begin
    l0: xor_gate port map (iQ(2), iQ(3), rez_xor);
    
    process (CLK, RESET)
    begin
        if RESET = '1' then
            iQ <= "1111";
        elsif rising_edge(CLK) then
            iQ(0) <= rez_xor;
            iQ(1) <= iQ(0);
            iQ(2) <= iQ(1);
            iQ(3) <= iQ(2);
        end if;
    end process;

    Q <= iQ;

end arch_lfsr4;




library IEEE;
use IEEE.STD_LOGIC_1164.all;

entity xor_gate is

	port (x, y: in STD_LOGIC;
	z: out STD_LOGIC);
	
end xor_gate;

architecture arch of xor_gate is
begin

	process(x, y)
	
	begin
	
		z<= x xor y;
	end process;
	
end arch;

// VHDL entity lfsr_8bit, as the project stores it:
library ieee;
use ieee.std_logic_1164.all;

entity lfsr_8bit is
  port(
    CLK   : in  std_logic;
    RESET : in  std_logic;
    Q     : out std_logic_vector(7 downto 0)
  );
end entity lfsr_8bit;

architecture arch_lfsr8 of lfsr_8bit is
  component xor_gate is
    port (
      x : in  std_logic;
      y : in  std_logic;
      z : out std_logic
    );
  end component xor_gate;

  signal iQ    : std_logic_vector(7 downto 0):="11111111";
  signal xor1  : std_logic;
  signal xor2  : std_logic;
  signal xor3  : std_logic;

begin
l0: xor_gate port map (iQ(1), iQ(5), xor1);
l1: xor_gate port map (iQ(6), iQ(7), xor2);
l3: xor_gate port map (xor1, xor2, xor3);
    
    process (CLK, RESET)
    begin
        if RESET = '1' then
            iQ <= "11111111";
        elsif rising_edge(CLK) then
            iQ(0) <=xor3;
            iQ(1) <= iQ(0);
            iQ(2) <= iQ(1);
            iQ(3) <= iQ(2);
            iQ(4) <= iQ(3);
            iQ(5) <= iQ(4);
            iQ(6) <= iQ(5);
            iQ(7) <= iQ(6);
        end if;
    end process;

    Q <= iQ;


end architecture arch_lfsr8;


library ieee;
use ieee.std_logic_1164.all;
use ieee.std_logic_arith.all;
use ieee.std_logic_unsigned.all;

entity xor_gate is

	port (x, y: in STD_LOGIC;
	z: out STD_LOGIC);
	
end xor_gate;

architecture arch_xor of xor_gate is
begin

	process(x, y)
	
	begin
	
		z<= x xor y;
	end process;
	
end arch_xor;

// VHDL entity data_generator_block, as the project stores it:
library ieee;
use ieee.std_logic_1164.all;
use ieee.numeric_std.all;
entity data_generator_block is
    port (
        CONTROL : in  std_logic_vector(1 downto 0);
        CLK     : in  std_logic;
        RESET   : in  std_logic;
        Data    : out std_logic_vector(7 downto 0)
    );
end entity data_generator_block;

architecture arch_data of data_generator_block is

    component lfsr_8bit is
        port (
            CLK   : in  std_logic;
            RESET : in  std_logic;
            Q     : out std_logic_vector(7 downto 0)
        );
    end component;
    
    component lfsr_4bit is
        port (
            CLK   : in  std_logic;
            Q     : out std_logic_vector(3 downto 0);
            RESET : in  std_logic
        );
    end component;
   
    signal iQ4  : std_logic_vector(3 downto 0);
    signal iQ8  : std_logic_vector(7 downto 0);
    signal iData: std_logic_vector(7 downto 0) := (others => '0');
    type rom_array is array (5 downto 0) of std_logic_vector(7 downto 0);
    constant student1data : rom_array := (
        "00001001",
        "00000111",
        "00000000",
        "00000010",
        "00001000",
        "00000001");
    constant student2data : rom_array := (
        "00001000",
        "00000011",
        "00000111",
        "00000110",
        "00000000",
        "00000101");
    
begin

    C0: lfsr_4bit port map (CLK, iQ4, RESET);
    C1: lfsr_8bit port map (CLK, RESET, iQ8);
    
    
    process (RESET, iQ4, iQ8, CONTROL,CLK)
    variable var:integer:=0;
    variable var2:integer:=0;
    begin
        if RESET = '1' then 
            iData <= (others => '0');
            var:=0;
             var2:=0;
            
        else
            case CONTROL is
               when "10" =>
                    var2:=0;
                   if rising_edge(CLK) then
                       if var< 6 then 
                       iData <= student1data(var);
                       var:=var+1;
                       else 
                         var:=0;
                         iData <= student1data(var);
                         var:=var+1;
                         end if;
                         end if;
                when "11" =>
                    var:=0;
                    if rising_edge(CLK) then
                       if var2< 6 then 
                       	iData <= student2data(var2);
                       	var2:=var2+1;
                       else 
                         var2:=0;
                         iData <= student2data(var2);
                         var2:=var2+1;
                       end if;
				end if;
                when "01" =>
                	var:=0;
                	var2:=0;
                    iData <= "0000" & iQ4;
                when others =>
                	var:=0;
                	var2:=0;
                    iData <= iQ8;
            end case;
        end if;
    end process;

    Data <= iData;
    
end architecture arch_data;


library ieee;
use ieee.std_logic_1164.all;

entity lfsr_4bit is
    port (
        CLK   : in  std_logic;
        Q     : out std_logic_vector(3 downto 0);
        RESET : in  std_logic
    );
end lfsr_4bit;

architecture arch_lfsr4 of lfsr_4bit is
    

    component xor_gate is
        port (
            x : in  std_logic;
            y : in  std_logic;
            z : out std_logic
        );
    end component;

    signal iQ      : std_logic_vector(3 downto 0) := "1111";
    signal rez_xor : std_logic;

begin
    l0: xor_gate port map (iQ(2), iQ(3), rez_xor);
    
    process (CLK, RESET)
    begin
        if RESET = '1' then
            iQ <= "1111";
        elsif rising_edge(CLK) then
            iQ(0) <= rez_xor;
            iQ(1) <= iQ(0);
            iQ(2) <= iQ(1);
            iQ(3) <= iQ(2);
        end if;
    end process;

    Q <= iQ;

end arch_lfsr4;




library IEEE;
use IEEE.STD_LOGIC_1164.all;

entity xor_gate is

	port (x, y: in STD_LOGIC;
	z: out STD_LOGIC);
	
end xor_gate;

architecture arch of xor_gate is
begin

	process(x, y)
	
	begin
	
		z<= x xor y;
	end process;
	
end arch;

library ieee;
use ieee.std_logic_1164.all;

entity lfsr_8bit is
  port(
    CLK   : in  std_logic;
    RESET : in  std_logic;
    Q     : out std_logic_vector(7 downto 0)
  );
end entity lfsr_8bit;

architecture arch_lfsr8 of lfsr_8bit is
  component xor_gate is
    port (
      x : in  std_logic;
      y : in  std_logic;
      z : out std_logic
    );
  end component xor_gate;

  signal iQ    : std_logic_vector(7 downto 0):="11111111";
  signal xor1  : std_logic;
  signal xor2  : std_logic;
  signal xor3  : std_logic;

begin
l0: xor_gate port map (iQ(1), iQ(5), xor1);
l1: xor_gate port map (iQ(6), iQ(7), xor2);
l3: xor_gate port map (xor1, xor2, xor3);
    
    process (CLK, RESET)
    begin
        if RESET = '1' then
            iQ <= "11111111";
        elsif rising_edge(CLK) then
            iQ(0) <=xor3;
            iQ(1) <= iQ(0);
            iQ(2) <= iQ(1);
            iQ(3) <= iQ(2);
            iQ(4) <= iQ(3);
            iQ(5) <= iQ(4);
            iQ(6) <= iQ(5);
            iQ(7) <= iQ(6);
        end if;
    end process;

    Q <= iQ;


end architecture arch_lfsr8;

library ieee;
use ieee.std_logic_1164.all;
use ieee.std_logic_arith.all;
use ieee.std_logic_unsigned.all;

entity xor_gate is

	port (x, y: in STD_LOGIC;
	z: out STD_LOGIC);
	
end xor_gate;

architecture arch_xor of xor_gate is
begin

	process(x, y)
	
	begin
	
		z<= x xor y;
	end process;
	
end arch_xor;

// VHDL entity frequency_divider, as the project stores it:
library ieee;
use ieee.std_logic_1164.all;
use ieee.numeric_std.all;

entity frequency_divider is
    port (
        clk     : in std_logic;
        R       : in std_logic;
        clk_out : out std_logic
    );
end frequency_divider;

architecture arch_freq of frequency_divider is
    signal count : unsigned(25 downto 0) := (others => '0');
begin
    process (clk, R)
    begin
        if R = '1' then
            count <= (others => '0');
        elsif rising_edge(clk) then
            count <= count + 1;
        end if;
    end process;

    clk_out <= count(25);
end arch_freq;

// VHDL entity average_2numbers, as the project stores it:
library ieee;
use ieee.std_logic_1164.all;
use ieee.std_logic_unsigned.all;

entity average_2numbers is
    port (
        nr1     : in  std_logic_vector(7 downto 0);
        nr2     : in  std_logic_vector(7 downto 0);
        average : out std_logic_vector(7 downto 0)
    );
end entity average_2numbers;

architecture arch_avg2 of average_2numbers is
    signal SUM : std_logic_vector(8 downto 0) := (others => '0');
begin 
    SUM <= ('0' & nr1) + ('0' & nr2);
    average <= SUM(8 downto 1);
end architecture arch_avg2;

// VHDL entity register_8bit, as the project stores it:
library ieee;
use ieee.std_logic_1164.all;

entity register_8bit is
    port (
        din : in std_logic_vector(7 downto 0);
        r   : in std_logic;
        clk : in std_logic;
        q   : out std_logic_vector(7 downto 0)
    );
end entity register_8bit;

architecture arch_registru of register_8bit is
    signal idin : std_logic_vector(7 downto 0) := (others => '0');
begin
    process (r, clk)
    begin
        if r = '1' then
            idin <= (others => '0');
        elsif rising_edge(clk) then
            idin <= din;
        end if;
    end process;

    q <= idin;
end architecture arch_registru;

// VHDL entity average_4numbers, as the project stores it:
library ieee;
use ieee.std_logic_1164.all;
use ieee.std_logic_unsigned.all;

entity average_4numbers is
    port (
        nr1 : in std_logic_vector(7 downto 0);
        nr2 : in std_logic_vector(7 downto 0);
        nr3 : in std_logic_vector(7 downto 0);
        nr4 : in std_logic_vector(7 downto 0);
        avg : out std_logic_vector(7 downto 0)
    );
end average_4numbers;

architecture arch_avg4 of average_4numbers is  
    signal first2_sum : std_logic_vector(8 downto 0);
    signal last2_sum  : std_logic_vector(8 downto 0);
    signal sum        : std_logic_vector(9 downto 0);
begin
    first2_sum <= ('0' & nr1) + ('0' & nr2);
    last2_sum  <= ('0' & nr3) + ('0' & nr4);
    sum        <= ('0' & first2_sum) + ('0' & last2_sum);
    avg        <= sum(9 downto 2);
end arch_avg4;

// VHDL entity average_8numbers, as the project stores it:
library ieee;
use ieee.std_logic_1164.all;
use ieee.std_logic_unsigned.all;

entity average_8numbers is
    port (
        nr1 : in std_logic_vector(7 downto 0);
        nr2 : in std_logic_vector(7 downto 0);
        nr3 : in std_logic_vector(7 downto 0);
        nr4 : in std_logic_vector(7 downto 0);
        nr5 : in std_logic_vector(7 downto 0);
        nr6 : in std_logic_vector(7 downto 0);
        nr7 : in std_logic_vector(7 downto 0);
        nr8 : in std_logic_vector(7 downto 0);
        avg : out std_logic_vector(7 downto 0)
    );
end average_8numbers;

architecture arch_avg8 of average_8numbers is

    signal sum_first2 : std_logic_vector(8 downto 0);
    signal sum_n3_n4  : std_logic_vector(8 downto 0);
    signal sum_n5_n6  : std_logic_vector(8 downto 0);
    signal sum_last2  : std_logic_vector(8 downto 0);
    signal sum        : std_logic_vector(10 downto 0);

begin

    sum_first2 <= ('0' & nr1) + ('0' & nr2);
    sum_n3_n4  <= ('0' & nr3) + ('0' & nr4);
    sum_n5_n6  <= ('0' & nr5) + ('0' & nr6);
    sum_last2  <= ('0' & nr7) + ('0' & nr8);
    
    sum <= ('0' & (('0' & sum_first2) + ('0' & sum_n3_n4))) + ('0' & (('0' & sum_n5_n6) + ('0' & sum_last2)));
    
    avg <= sum(10 downto 3);
	
end arch_avg8;

// VHDL entity average_16numbers, as the project stores it:
library ieee;
use ieee.std_logic_1164.all;
use ieee.std_logic_unsigned.all;
entity average_16numbers is
    port (
        nr1  : in std_logic_vector(7 downto 0);
        nr2  : in std_logic_vector(7 downto 0);
        nr3  : in std_logic_vector(7 downto 0);
        nr4  : in std_logic_vector(7 downto 0);
        nr5  : in std_logic_vector(7 downto 0);
        nr6  : in std_logic_vector(7 downto 0);
        nr7  : in std_logic_vector(7 downto 0);
        nr8  : in std_logic_vector(7 downto 0);
        nr9  : in std_logic_vector(7 downto 0);
        nr10 : in std_logic_vector(7 downto 0);
        nr11 : in std_logic_vector(7 downto 0);
        nr12 : in std_logic_vector(7 downto 0);
        nr13 : in std_logic_vector(7 downto 0);
        nr14 : in std_logic_vector(7 downto 0);
        nr15 : in std_logic_vector(7 downto 0);
        nr16 : in std_logic_vector(7 downto 0);
        avg  : out std_logic_vector(7 downto 0)
    );
end average_16numbers;

architecture arch_avg16 of average_16numbers is

    signal sum_nr1_nr2   : std_logic_vector(8 downto 0);
    signal sum_nr3_nr4   : std_logic_vector(8 downto 0);
    signal sum_nr5_nr6   : std_logic_vector(8 downto 0);
    signal sum_nr7_nr8   : std_logic_vector(8 downto 0);
    signal sum_nr9_nr10  : std_logic_vector(8 downto 0);
    signal sum_nr11_nr12 : std_logic_vector(8 downto 0);
    signal sum_nr13_nr14 : std_logic_vector(8 downto 0);
    signal sum_nr15_nr16 : std_logic_vector(8 downto 0);
    signal sum1_4        : std_logic_vector(9 downto 0);
    signal sum5_8        : std_logic_vector(9 downto 0);
    signal sum9_12       : std_logic_vector(9 downto 0);
    signal sum13_16      : std_logic_vector(9 downto 0);
    signal sum           : std_logic_vector(11 downto 0);

begin

    sum_nr1_nr2   <= ('0' & nr1)  + ('0' & nr2);
    sum_nr3_nr4   <= ('0' & nr3)  + ('0' & nr4);
    sum_nr5_nr6   <= ('0' & nr5)  + ('0' & nr6);
    sum_nr7_nr8   <= ('0' & nr7)  + ('0' & nr8);
    sum_nr9_nr10  <= ('0' & nr9)  + ('0' & nr10);
    sum_nr11_nr12 <= ('0' & nr11) + ('0' & nr12);
    sum_nr13_nr14 <= ('0' & nr13) + ('0' & nr14);
    sum_nr15_nr16 <= ('0' & nr15) + ('0' & nr16);
    
    sum1_4  <= ('0' & sum_nr1_nr2)   + ('0' & sum_nr3_nr4);
    sum5_8  <= ('0' & sum_nr5_nr6)   + ('0' & sum_nr7_nr8);
    sum9_12 <= ('0' & sum_nr9_nr10)  + ('0' & sum_nr11_nr12);
    sum13_16 <= ('0' & sum_nr13_nr14) + ('0' & sum_nr15_nr16);
    
    sum <= ('0' & (('0' & sum1_4) + ('0' & sum5_8))) + ('0' & (('0' & sum9_12) + ('0' & sum13_16)));
    
    avg <= sum(11 downto 4);
	
end arch_avg16;

// VHDL entity average_computer_block, as the project stores it:
library ieee;
use ieee.std_logic_1164.all;
use ieee.std_logic_unsigned.all;
USE ieee.std_logic_arith.all;
use ieee.numeric_std.all;

entity average_computer_block is
    port (
        DIN: in std_logic_vector(7 downto 0);
        CLK: in std_logic;
        FILTER: in std_logic_vector(1 downto 0);
        RESET: in std_logic;
        AVERAGE: out std_logic_vector(7 downto 0)
    );
end average_computer_block;

architecture arch_avg of average_computer_block is

    component average_16numbers is
        port (
             nr1  : in std_logic_vector(7 downto 0);
	        nr2  : in std_logic_vector(7 downto 0);
	        nr3  : in std_logic_vector(7 downto 0);
	        nr4  : in std_logic_vector(7 downto 0);
	        nr5  : in std_logic_vector(7 downto 0);
	        nr6  : in std_logic_vector(7 downto 0);
	        nr7  : in std_logic_vector(7 downto 0);
	        nr8  : in std_logic_vector(7 downto 0);
	        nr9  : in std_logic_vector(7 downto 0);
	        nr10 : in std_logic_vector(7 downto 0);
	        nr11 : in std_logic_vector(7 downto 0);
	        nr12 : in std_logic_vector(7 downto 0);
	        nr13 : in std_logic_vector(7 downto 0);
	        nr14 : in std_logic_vector(7 downto 0);
	        nr15 : in std_logic_vector(7 downto 0);
	        nr16 : in std_logic_vector(7 downto 0);
	        avg  : out std_logic_vector(7 downto 0)
        );
    end component;

    component average_2numbers is
        port (
            nr1: in std_logic_vector(7 downto 0);
            nr2: in std_logic_vector(7 downto 0);
            average: out std_logic_vector(7 downto 0)
        );
    end component;

    component average_4numbers is
        port (
            nr1: in std_logic_vector(7 downto 0);
            nr2: in std_logic_vector(7 downto 0);
            nr3: in std_logic_vector(7 downto 0);
            nr4: in std_logic_vector(7 downto 0);
            avg: out std_logic_vector(7 downto 0)
        );
    end component;

    component register_8bit is
        port (
            din: in std_logic_vector(7 downto 0);
            r: in std_logic;
            clk: in std_logic;
            q: out std_logic_vector(7 downto 0)
        );
    end component;

    component average_8numbers is
        port (
	       nr1 : in std_logic_vector(7 downto 0);
	       nr2 : in std_logic_vector(7 downto 0);
	       nr3 : in std_logic_vector(7 downto 0);
	       nr4 : in std_logic_vector(7 downto 0);
	       nr5 : in std_logic_vector(7 downto 0);
	       nr6 : in std_logic_vector(7 downto 0);
	       nr7 : in std_logic_vector(7 downto 0);
	       nr8 : in std_logic_vector(7 downto 0);
	       avg : out std_logic_vector(7 downto 0)
        );
    end component;

    type NUMBERS_TYPE is array (0 to 15) of std_logic_vector(7 downto 0);
    signal AVERAGE_LAST2: std_logic_vector(7 downto 0);
    signal AVERAGE_LAST4: std_logic_vector(7 downto 0);
    signal AVERAGE_LAST8: std_logic_vector(7 downto 0);
    signal AVERAGE_LAST16: std_logic_vector(7 downto 0);
    signal NUM: NUMBERS_TYPE;

begin

    Registers: for I in 0 to 15 generate
        L1: if I = 0 generate
            L2: register_8bit port map (DIN, RESET, CLK, NUM(0));
        end generate;

        L3: if I > 0 generate
            L3: register_8bit port map (NUM(I - 1), RESET, CLK, NUM(I));
        end generate;
    end generate;

    AVG_OF_LAST2: average_2numbers port map (NUM(0), NUM(1), AVERAGE_LAST2);
    AVG_OF_LAST4: average_4numbers port map (NUM(0), NUM(1), NUM(2), NUM(3), AVERAGE_LAST4);
    AVG_OF_LAST8: average_8numbers port map (NUM(0), NUM(1), NUM(2), NUM(3), NUM(4), NUM(5), NUM(6), NUM(7), AVERAGE_LAST8);
    AVG_OF_LAST16: average_16numbers port map (NUM(0), NUM(1), NUM(2), NUM(3), NUM(4), NUM(5), NUM(6), NUM(7),NUM(8), NUM(9), NUM(10), NUM(11), NUM(12), NUM(13), NUM(14), NUM(15), AVERAGE_LAST16);

    process (FILTER, AVERAGE_LAST2, AVERAGE_LAST4, AVERAGE_LAST8, AVERAGE_LAST16)
        variable AVG: std_logic_vector(7 downto 0) := "00000000";
    begin
        case FILTER is
            when "00" =>
                AVG := AVERAGE_LAST2;
            when "01" =>
                AVG := AVERAGE_LAST4;
            when "10" =>
                AVG := AVERAGE_LAST8;
            when "11" =>
                AVG := AVERAGE_LAST16;
            when others =>
                null;
        end case;

        AVERAGE <= AVG;
    end process;

end arch_avg;

library ieee;
use ieee.std_logic_1164.all;

entity register_8bit is
    port (
        din : in std_logic_vector(7 downto 0);
        r   : in std_logic;
        clk : in std_logic;
        q   : out std_logic_vector(7 downto 0)
    );
end entity register_8bit;

architecture arch_registru of register_8bit is
    signal idin : std_logic_vector(7 downto 0) := (others => '0');
begin
    process (r, clk)
    begin
        if r = '1' then
            idin <= (others => '0');
        elsif rising_edge(clk) then
            idin <= din;
        end if;
    end process;

    q <= idin;
end architecture arch_registru;


library ieee;
use ieee.std_logic_1164.all;
use ieee.std_logic_unsigned.all;

entity average_2numbers is
    port (
        nr1     : in  std_logic_vector(7 downto 0);
        nr2     : in  std_logic_vector(7 downto 0);
        average : out std_logic_vector(7 downto 0)
    );
end entity average_2numbers;

architecture arch_avg2 of average_2numbers is
    signal SUM : std_logic_vector(8 downto 0) := (others => '0');
begin 
    SUM <= ('0' & nr1) + ('0' & nr2);
    average <= SUM(8 downto 1);
end architecture arch_avg2;


library ieee;
use ieee.std_logic_1164.all;
use ieee.std_logic_unsigned.all;

entity average_4numbers is
    port (
        nr1 : in std_logic_vector(7 downto 0);
        nr2 : in std_logic_vector(7 downto 0);
        nr3 : in std_logic_vector(7 downto 0);
        nr4 : in std_logic_vector(7 downto 0);
        avg : out std_logic_vector(7 downto 0)
    );
end average_4numbers;

architecture arch_avg4 of average_4numbers is  
    signal first2_sum : std_logic_vector(8 downto 0);
    signal last2_sum  : std_logic_vector(8 downto 0);
    signal sum        : std_logic_vector(9 downto 0);
begin
    first2_sum <= ('0' & nr1) + ('0' & nr2);
    last2_sum  <= ('0' & nr3) + ('0' & nr4);
    sum        <= ('0' & first2_sum) + ('0' & last2_sum);
    avg        <= sum(9 downto 2);
end arch_avg4;

library ieee;
use ieee.std_logic_1164.all;
use ieee.std_logic_unsigned.all;

entity average_8numbers is
    port (
        nr1 : in std_logic_vector(7 downto 0);
        nr2 : in std_logic_vector(7 downto 0);
        nr3 : in std_logic_vector(7 downto 0);
        nr4 : in std_logic_vector(7 downto 0);
        nr5 : in std_logic_vector(7 downto 0);
        nr6 : in std_logic_vector(7 downto 0);
        nr7 : in std_logic_vector(7 downto 0);
        nr8 : in std_logic_vector(7 downto 0);
        avg : out std_logic_vector(7 downto 0)
    );
end average_8numbers;

architecture arch_avg8 of average_8numbers is

    signal sum_first2 : std_logic_vector(8 downto 0);
    signal sum_n3_n4  : std_logic_vector(8 downto 0);
    signal sum_n5_n6  : std_logic_vector(8 downto 0);
    signal sum_last2  : std_logic_vector(8 downto 0);
    signal sum        : std_logic_vector(10 downto 0);

begin

    sum_first2 <= ('0' & nr1) + ('0' & nr2);
    sum_n3_n4  <= ('0' & nr3) + ('0' & nr4);
    sum_n5_n6  <= ('0' & nr5) + ('0' & nr6);
    sum_last2  <= ('0' & nr7) + ('0' & nr8);
    
    sum <= ('0' & (('0' & sum_first2) + ('0' & sum_n3_n4))) + ('0' & (('0' & sum_n5_n6) + ('0' & sum_last2)));
    
    avg <= sum(10 downto 3);
	
end arch_avg8;

library ieee;
use ieee.std_logic_1164.all;
use ieee.std_logic_unsigned.all;
entity average_16numbers is
    port (
        nr1  : in std_logic_vector(7 downto 0);
        nr2  : in std_logic_vector(7 downto 0);
        nr3  : in std_logic_vector(7 downto 0);
        nr4  : in std_logic_vector(7 downto 0);
        nr5  : in std_logic_vector(7 downto 0);
        nr6  : in std_logic_vector(7 downto 0);
        nr7  : in std_logic_vector(7 downto 0);
        nr8  : in std_logic_vector(7 downto 0);
        nr9  : in std_logic_vector(7 downto 0);
        nr10 : in std_logic_vector(7 downto 0);
        nr11 : in std_logic_vector(7 downto 0);
        nr12 : in std_logic_vector(7 downto 0);
        nr13 : in std_logic_vector(7 downto 0);
        nr14 : in std_logic_vector(7 downto 0);
        nr15 : in std_logic_vector(7 downto 0);
        nr16 : in std_logic_vector(7 downto 0);
        avg  : out std_logic_vector(7 downto 0)
    );
end average_16numbers;

architecture arch_avg16 of average_16numbers is

    signal sum_nr1_nr2   : std_logic_vector(8 downto 0);
    signal sum_nr3_nr4   : std_logic_vector(8 downto 0);
    signal sum_nr5_nr6   : std_logic_vector(8 downto 0);
    signal sum_nr7_nr8   : std_logic_vector(8 downto 0);
    signal sum_nr9_nr10  : std_logic_vector(8 downto 0);
    signal sum_nr11_nr12 : std_logic_vector(8 downto 0);
    signal sum_nr13_nr14 : std_logic_vector(8 downto 0);
    signal sum_nr15_nr16 : std_logic_vector(8 downto 0);
    signal sum1_4        : std_logic_vector(9 downto 0);
    signal sum5_8        : std_logic_vector(9 downto 0);
    signal sum9_12       : std_logic_vector(9 downto 0);
    signal sum13_16      : std_logic_vector(9 downto 0);
    signal sum           : std_logic_vector(11 downto 0);

begin

    sum_nr1_nr2   <= ('0' & nr1)  + ('0' & nr2);
    sum_nr3_nr4   <= ('0' & nr3)  + ('0' & nr4);
    sum_nr5_nr6   <= ('0' & nr5)  + ('0' & nr6);
    sum_nr7_nr8   <= ('0' & nr7)  + ('0' & nr8);
    sum_nr9_nr10  <= ('0' & nr9)  + ('0' & nr10);
    sum_nr11_nr12 <= ('0' & nr11) + ('0' & nr12);
    sum_nr13_nr14 <= ('0' & nr13) + ('0' & nr14);
    sum_nr15_nr16 <= ('0' & nr15) + ('0' & nr16);
    
    sum1_4  <= ('0' & sum_nr1_nr2)   + ('0' & sum_nr3_nr4);
    sum5_8  <= ('0' & sum_nr5_nr6)   + ('0' & sum_nr7_nr8);
    sum9_12 <= ('0' & sum_nr9_nr10)  + ('0' & sum_nr11_nr12);
    sum13_16 <= ('0' & sum_nr13_nr14) + ('0' & sum_nr15_nr16);
    
    sum <= ('0' & (('0' & sum1_4) + ('0' & sum5_8))) + ('0' & (('0' & sum9_12) + ('0' & sum13_16)));
    
    avg <= sum(11 downto 4);
	
end arch_avg16;

// VHDL entity lcd_display, as the project stores it:
library IEEE;
use IEEE.STD_LOGIC_1164.all;
use ieee.std_logic_unsigned.all;

entity lcd_display is
    port (
        CLK, RESET: in std_logic;
        DIN, AVG: in std_logic_vector(7 downto 0);
        ANODE: out std_logic_vector(3 downto 0);
        CATHODE: out std_logic_vector(6 downto 0)
    );
end lcd_display;

architecture arch of lcd_display is

    signal LED_BCD : std_logic_vector(3 downto 0);
    signal led_count : std_logic_vector(1 downto 0);

begin
    process(LED_BCD)
    begin
        case LED_BCD is
            when "0000" => CATHODE <= "0000001"; -- "0"
            when "0001" => CATHODE <= "1001111"; -- "1"
            when "0010" => CATHODE <= "0010010"; -- "2"
            when "0011" => CATHODE <= "0000110"; -- "3"
            when "0100" => CATHODE <= "1001100"; -- "4"
            when "0101" => CATHODE <= "0100100"; -- "5"
            when "0110" => CATHODE <= "0100000"; -- "6"
            when "0111" => CATHODE <= "0001111"; -- "7"
            when "1000" => CATHODE <= "0000000"; -- "8"
            when "1001" => CATHODE <= "0000100"; -- "9"
            when "1010" => CATHODE <= "0001000"; -- "A"
            when "1011" => CATHODE <= "1100000"; -- "B"
            when "1100" => CATHODE <= "0110001"; -- "C"
            when "1101" => CATHODE <= "1000010"; -- "D"
            when "1110" => CATHODE <= "0110000"; -- "E"
            when "1111" => CATHODE <= "0111000"; -- "F"
            when others => CATHODE <= "1111111"; -- "LCD off"
        end case;
    end process;

    process (CLK, RESET)
        variable divider : INTEGER := 0;
    begin
        if RESET = '1' then
            led_count <= "00";
        else
            if (rising_edge(CLK)) then
                divider := divider + 1;
                if (divider = 10000) then
                    led_count <= led_count + 1;
                    divider := 0;
                end if;
            end if;
        end if;
    end process;

    process (led_count, DIN, AVG)
    begin
        case led_count is
            when "00" =>
                LED_BCD <= DIN(7 downto 4);
                ANODE <= "0111";
            when "01" =>
                LED_BCD <= DIN(3 downto 0);
                ANODE <= "1011";
            when "10" =>
                LED_BCD <= AVG(7 downto 4);
                ANODE <= "1101";
            when "11" =>
                LED_BCD <= AVG(3 downto 0);
                ANODE <= "1110";
            when others =>
                ANODE <= "1111";
        end case;
    end process;

end arch;

// VHDL entity commanding_unit, as the project stores it:
library IEEE;
use IEEE.std_logic_1164.all;

entity commanding_unit is
    port (
        SYSTEM_CLK: in std_logic;
        RESET: in std_logic;
        CONTROL: in std_logic_vector(1 downto 0);
        FILTER: in std_logic_vector(1 downto 0);
        CATHODE: out std_logic_vector(6 downto 0);
        ANODE: out std_logic_vector(3 downto 0);
        SQW: in std_logic
    );
end commanding_unit;

architecture arch of commanding_unit is

    signal CLK_1HZ : std_logic;
    signal CLK_SQUARE_WAVE : std_logic;
    signal CLK : std_logic;
    signal DIN : std_logic_vector(7 downto 0);
    signal AVG : std_logic_vector(7 downto 0);

    component frequency_divider is
        port (
            CLK_IN: in std_logic;
            RESET: in std_logic;
            CLK_OUT: out std_logic
        );
    end component;

    component data_generator_block is
        port (
            CLK: in std_logic;
            RESET: in std_logic;
            CONTROL: in std_logic_vector(1 downto 0);
            DATA: out std_logic_vector(7 downto 0)
        );
    end component;

    component average_computer_block is
        port (
            DIN: in std_logic_vector(7 downto 0);
            CLK: in std_logic;
            FILTER: in std_logic_vector(1 downto 0);
            RESET: in std_logic;
            AVERAGE: out std_logic_vector(7 downto 0)
        );
    end component;

    component lcd_display is
        port (
            CLK, RESET: in std_logic;
            DIN, AVG: in std_logic_vector(7 downto 0);
            ANODE: out std_logic_vector(3 downto 0);
            CATHODE: out std_logic_vector(6 downto 0)
        );
    end component;

    component squarewave_generator is
        port (
            CLK_IN: in std_logic;
            RESET: in std_logic;
            CLK_OUT: out std_logic
        );
    end component;

begin
    L1: frequency_divider port map(SYSTEM_CLK, RESET, CLK_1HZ);
    L2: data_generator_block port map(CLK, RESET, CONTROL, DIN);
    L3: average_computer_block port map(DIN, CLK, FILTER, RESET, AVG);
    L4: squarewave_generator port map(CLK_1HZ, RESET, CLK_SQUARE_WAVE);
    L5: lcd_display port map(SYSTEM_CLK, RESET, DIN, AVG, ANODE, CATHODE);

    process(SQW)
    begin
        if SQW = '0' then
            CLK <= CLK_1HZ;
        else
            CLK <= CLK_SQUARE_WAVE;
        end if;
    end process;
end arch;

// VHDL entity decodificator_zecimal, as the project stores it:
library ieee;
use ieee.std_logic_1164.all;
use ieee.std_logic_unsigned.all;
use ieee.numeric_std.all;

entity decodificator_zecimal is
  port (
    nr_bin: in std_logic_vector(7 downto 0);
    Unitate: out std_logic_vector(3 downto 0);
    Zecimala: out std_logic_vector(3 downto 0);
    Sute: out std_logic_vector(3 downto 0)
  );
end decodificator_zecimal;

architecture comport of decodificator_zecimal is
  signal num_int: integer := 0;
  signal u, z, s,copy: integer := 0;
begin
  num_int <= to_integer(unsigned(nr_bin));
  copy<=num_int;
  s <= num_int /100;
  z <= (num_int/10)mod 10;
  u <= num_int mod 10;
  process(s)
  begin
    case s is
      when 0 => Sute <= "0000";
      when 1 => Sute <= "0001";
      when 2 => Sute <= "0010";
      when 3 => Sute <= "0011";
      when 4 => Sute <= "0100";
      when 5 => Sute <= "0101";
      when 6 => Sute <= "0110";
      when 7 => Sute <= "0111";
      when 8 => Sute <= "1000";
      when 9 => Sute <= "1001";
      when others => Sute <= "0000";
    end case;
  end process;
  

  process(u)
  begin
    case u is
      when 0 => Unitate <= "0000";
      when 1 => Unitate <= "0001";
      when 2 => Unitate <= "0010";
      when 3 => Unitate <= "0011";
      when 4 => Unitate <= "0100";
      when 5 => Unitate <= "0101";
      when 6 => Unitate <= "0110";
      when 7 => Unitate <= "0111";
      when 8 => Unitate <= "1000";
      when 9 => Unitate <= "1001";
      when others => Unitate <= "0000";
    end case;
  end process;

  process(z)
  begin
    case z is
      when 0 => Zecimala <= "0000";
      when 1 => Zecimala <= "0001";
      when 2 => Zecimala <= "0010";
      when 3 => Zecimala <= "0011";
      when 4 => Zecimala <= "0100";
      when 5 => Zecimala <= "0101";
      when 6 => Zecimala <= "0110";
      when 7 => Zecimala <= "0111";
      when 8 => Zecimala <= "1000";
      when 9 => Zecimala <= "1001";
      when others => Zecimala <= "0000";
    end case;
  end process;
end comport;

// VHDL entity hex_7seg, as the project stores it:
library ieee;
use ieee.std_logic_1164.all;

entity hex_7seg is
  port (
    hex_in: in std_logic_vector(3 downto 0);
    a_b_c_d_e_f_g: out std_logic_vector(6 downto 0)
  );
end hex_7seg;

architecture arch_hex of hex_7seg is
begin
  process(hex_in)
  begin
    case hex_in is
      when "0000" => a_b_c_d_e_f_g <= "1111110";
      when "0001" => a_b_c_d_e_f_g <= "0110000";
      when "0010" => a_b_c_d_e_f_g <= "1101101";
      when "0011" => a_b_c_d_e_f_g <= "1111001";
      when "0100" => a_b_c_d_e_f_g <= "0110011";
      when "0101" => a_b_c_d_e_f_g <= "1011011";
      when "0110" => a_b_c_d_e_f_g <= "1011111";
      when "0111" => a_b_c_d_e_f_g <= "1110000";
      when "1000" => a_b_c_d_e_f_g <= "1111111";
      when "1001" => a_b_c_d_e_f_g <= "1111011";
      when "1010" => a_b_c_d_e_f_g <= "1110111";
      when "1011" => a_b_c_d_e_f_g <= "0011111";
      when "1100" => a_b_c_d_e_f_g <= "1001110";
      when "1101" => a_b_c_d_e_f_g <= "0111101";
      when "1110" => a_b_c_d_e_f_g <= "1001111";
      when "1111" => a_b_c_d_e_f_g <= "0000001";
      when others => a_b_c_d_e_f_g <= "0000000";
    end case;
  end process;
end arch_hex;
